// Digital circuit full_adder.dig as structural Verilog
module full_adder (
  input  A,
  input  B,
  input  C_IN,
  output S,
  output C_OUT
);

  wire and_1_out, and_2_out, xor_1_out;

  xor xor_1 (xor_1_out, A, B);
  and and_1 (and_1_out, A, B);
  xor xor_2 (S, xor_1_out, C_IN);
  and and_2 (and_2_out, xor_1_out, C_IN);
  or or_1 (C_OUT, and_2_out, and_1_out);
endmodule
